# Fritzing sketch AirQ (saved by Fritzing 0.9.10b)
circuit board: 8.46667cm x 5.64444cm
breadboards: 1

parts:
  ESP-LORA32 = Heltec WiFi LoRa 32 V2 [part_number=HTIT-WB32LA]
  PMS5003 = PMS5003
  MQ135 = Gas Sensor Breakout Board
  MQ9 = Gas Sensor Breakout Board
  MQ5 = Gas Sensor Breakout Board
  DHT11 = DHT11 Humitidy and Temperature Sensor

nets:
  N1: ESP-LORA32.pin_2, MQ5.A1, MQ5.A2
  N2: ESP-LORA32.pin_3, MQ9.A1, MQ9.A2
  N3: ESP-LORA32.pin_4, MQ135.A1, MQ135.A2
  N4: ESP-LORA32.pin_16, ESP-LORA32.pin_17, MQ135.H1, MQ9.H1, MQ5.H1, DHT11.VDD
  GND: ESP-LORA32.GND, PMS5003.Pin_2, MQ135.GND, MQ9.GND, MQ5.GND, DHT11.GND
  N5: ESP-LORA32.pin_20, PMS5003.Pin_1
  N6: ESP-LORA32.pin_21, ESP-LORA32.pin_22
  N7: ESP-LORA32.pin_26, PMS5003.Pin_4
  N8: ESP-LORA32.pin_32, DHT11.DATA
  N9: ESP-LORA32.pin_33, PMS5003.Pin_5

custom parts:
  PMS5003: PMS5003 is a kind of digital and universal particle concentration sensor, which can be used to obtain the number of suspended particles in the air.
  DHT11 Humitidy and Temperature Sensor: DHT11 Humidity and Temperature Sensor
